# Fritzing sketch Zoltar_init (saved by Fritzing 0.9.3b)
breadboards: 1

parts:
  Part1 = Arduino Mega 2560 (Rev3)
  DFRobot_DFPlayer_Mini1 = DFRobot DFPlayer Mini [part_number=DFR0299]
  R1 = Resistor [tolerance=±5% resistance=1k package="2010 [SMD]"]
  R2 = Resistor [tolerance=±5% resistance=10k package=THT]
  S1 = Momentary Switch [package=ksa_sealed_tac_switch]

nets:
  N1: Part1.D15/RX3, DFRobot_DFPlayer_Mini1.TX
  N2: Part1.D14/TX3, R1.Pin_0
  N3: Part1.GND, DFRobot_DFPlayer_Mini1.GND-1, DFRobot_DFPlayer_Mini1.GND-2, R2.Pin_1
  5V: Part1.5V, DFRobot_DFPlayer_Mini1.VCC, S1.4
  N4: Part1.D7_PWM, S1.1
  N5: DFRobot_DFPlayer_Mini1.RX, R1.Pin_1
  N6: R2.Pin_0, S1.2

// code stored in the sketch: Zoldar.ino
#include "Arduino.h"
#include "SoftwareSerial.h"
#include "DFRobotDFPlayerMini.h"
#include "Configuration.h"

DFRobotDFPlayerMini myDFPlayer;

int status;
boolean isStatusInit;
SoftwareSerial musicSoftwareSerial(MUSIC_RX_PIN, MUSIC_TX_PIN); // RX, TX

void setup() {
    isStatusInit = false;
    
    Serial.begin(9600);
    initMusicConfiguration();  
    
    status = STATUS_STAND_BY;
    pinMode(DETECT_COIN_PIN, INPUT);
} 

void loop() {

  //printStatus();

  switch (status) {

    case STATUS_INIT:
      statusInit();
      break;

    case STATUS_ACTIVATE_GAME:
      // Encender luces "Apunta a la boca"
      // Encender sonido campana
      // Activar los mandos
      //delay(10000);
      
      statusActivateGame();
      
      // Desactivar los mandos
      // Encender luces "Pulsa botón liberar moneda"
      // Activo siguiente estado WAITING_RELEASE_COIN

      break;

    case STATUS_WAITING_RELEASE_COIN:
      // Esperamos 10 segundos comprobando si se ha pulsado el botón de "liberar moneda"
      // Cuando se ha pulsado el botón o hayan pasado los 10 segundos, se libera la moneda.
      // Activo siguiente estado WIN_OR_LOST
      break;

    case STATUS_WIN_OR_LOST:
      // Chequeamos los sensores de acierto o no
      // Si ha acertado pasamos a "WIN" sino a "LOST"
      break;

    case STATUS_WIN:
        // Sacar tarjeta Acierto
        // Activar siguiente estado OFF
      break;

    case STATUS_LOST:
        // Sacar tarjeta de la tienda
        // Activar siguiente estado OFF
      break;

    case STATUS_OFF:
        // Esperar a que termine la música
        // desactivar musica y luces y movimiento. Todo
        // Activar siguiente estado STAND_BY
      break;

    default: //case "STAND_BY":
      statusStandBy();
      break;

  }
}


void initMusicConfiguration() {

  musicSoftwareSerial.begin(9600);
    if (!myDFPlayer.begin(musicSoftwareSerial)) {  //Use softwareSerial to communicate with mp3.
      while(true);
    }
    myDFPlayer.volume(MUSIC_VOLUME);
}

void playMusic() {
  myDFPlayer.play(1);  //Play the first mp3
}

// Input: Detectar moneda
void statusStandBy() {

  // Esperando a que llegue la señal de la moneda
  // Y cambio al siguiente estado INIT

  int inputCoin = digitalRead(DETECT_COIN_PIN);
  Serial.println(inputCoin);
  if (inputCoin == HIGH) {
    //status = STATUS_INIT;
  }
}

// Input: Play música
// Output: Led fondo
// Output: Led ojos
// Output: Mover boca
void statusInit() {
  Serial.println("statusInit");
  // Encender luces de fondo
  // Encender ojos
  // Encender movimiento de boca
  if (isStatusInit == false) {

    playMusic();
    backgroundLedOn();
    eyesLedOn();
    mouthMoveOn();
    
    isStatusInit = true;

    delay(DELAY_AFTER_STATUS_INIT);
  
    // cambiamos al siguiente estado ACTIVATE_GAME
    status = STATUS_ACTIVATE_GAME;
  }  
}

void statusActivateGame() {
  

}


void backgroundLedOn() {  
  
  
}

void eyesLedOn() {
  
  
}

void mouthMoveOn() {
  
  
}


void printStatus() {

  String statusText = "STAND_BY";

  switch (status) {
    
    case STATUS_INIT:
      statusText = "INIT";
    break;
    case STATUS_ACTIVATE_GAME:
      statusText = "ACTIVATE_GAME";
    break;
    case STATUS_WAITING_RELEASE_COIN:
      statusText = "WAITING_RELEASE_COIN";
    break;
    case STATUS_WIN_OR_LOST:
      statusText = "WIN_OR_LOST";
    break;
    case STATUS_WIN:
      statusText = "WIN";
    break;
    case STATUS_LOST:
      statusText = "LOST";
    break;
    case STATUS_OFF:
      statusText = "OFF";
    break;
    default:
      statusText = "STAND_BY";
    break;
  }


    Serial.println("STATUS :" + statusText);

}

// code stored in the sketch: Zoltar_init_2.ino
#include "Arduino.h"
#include "DFRobotDFPlayerMini.h"

DFRobotDFPlayerMini myDFPlayer;


const int STATUS_STAND_BY = -1;
const int STATUS_INIT = 0;
const int STATUS_ACTIVATE_GAME = 1;
const int STATUS_WAITING_RELEASE_COIN = 2;
const int STATUS_WIN_OR_LOST = 3;
const int STATUS_WIN = 4;
const int STATUS_LOST = 5;
const int STATUS_OFF = 6;

const int INIT_BUTTON_PIN = 7;

int status;

void setup() {
		status = STATUS_STAND_BY;
		pinMode(INIT_BUTTON_PIN, INPUT);
} 

void loop() {


	switch (status) {

    case STATUS_INIT:
			// Encender luces de fondo
			// Encender ojos
			// Encender movimiento de boca
			initMusic();
			delay(5000);
			// cambiamos al siguiente estado ACTIVATE_GAME
      break;

    case STATUS_ACTIVATE_GAME:
			// Encender luces "Apunta a la boca"
			// Encender sonido campana
			// Activar los mandos
			delay(10000);

			// Desactivar los mandos
			// Encender luces "Pulsa botón liberar moneda"
			// Activo siguiente estado WAITING_RELEASE_COIN

      break;

    case STATUS_WAITING_RELEASE_COIN:
			// Esperamos 10 segundos comprobando si se ha pulsado el botón de "liberar moneda"
			// Cuando se ha pulsado el botón o hayan pasado los 10 segundos, se libera la moneda.
			// Activo siguiente estado WIN_OR_LOST
      break;

		case STATUS_WIN_OR_LOST:
			// Chequeamos los sensores de acierto o no
			// Si ha acertado pasamos a "WIN" sino a "LOST"
      break;

		case STATUS_WIN:
				// Sacar tarjeta Acierto
				// Activar siguiente estado OFF
      break;

		case STATUS_LOST:
				// Sacar tarjeta de la tienda
				// Activar siguiente estado OFF
      break;

		case STATUS_OFF:
				// Esperar a que termine la música
				// desactivar musica y luces y movimiento. Todo
				// Activar siguiente estado STAND_BY
			break;

    default: //case "STAND_BY":
			standBy();
      break;

  }
}

void standBy() {

	// Esperando a que llegue la señal de la moneda
	// Y cambio al siguiente estado INIT

	int inputButton = digitalRead(INIT_BUTTON_PIN);
	Serial.println(inputButton);



}

void initMusic() {
	Serial.begin(9600);
  
  if (!myDFPlayer.begin(Serial)) {  //Use softwareSerial to communicate with mp3.
    while(true);
  }
  
  myDFPlayer.volume(30);  //Set volume value. From 0 to 30
  myDFPlayer.play(1);  //Play the first mp3
}
